# Fritzing sketch rc-car (saved by Fritzing 0.9.3b)
breadboards: 1

parts:
  IC1 = L293D [package=THT]
  Raspberry_Pi1 = Raspberry Pi B rev2
  VCC1 = 4 x AAA Battery Mount
  Grove1 = Grove 3 Axis Digital Accelerometer 16g
  M1 = DC Motor  # not connected
  M2 = DC Motor
  M3 = DC Motor  # not connected
  M4 = DC Motor

nets:
  N1: IC1.Enable_1, Raspberry_Pi1.GPIO_25
  N2: IC1.In_1, Raspberry_Pi1.GPIO_24
  N3: IC1.Out_1_(_Controlled_by_Enable_1_), M4.pin_2
  N4: IC1.0V, IC1.+Vmotor, IC1.+V, Raspberry_Pi1.5V, VCC1.+
  N5: IC1.Out_2_(_Controlled_by_Enable_1_), M4.pin_1
  N6: IC1.In_2, Raspberry_Pi1.GPIO_23
  N7: IC1.Enable_2, Raspberry_Pi1.GPIO_17
  N8: IC1.In_3, Raspberry_Pi1.GPIO_22
  N9: IC1.Out_3_(_Controlled_by_Enable_2_), M2.pin_1
  N10: IC1.Out_4_(_Controlled_by_Enable_2_), M2.pin_2
  N11: IC1.In_4, Raspberry_Pi1.GPIO_27
  3V3: Raspberry_Pi1.3V3, Grove1.VCC
  N12: Raspberry_Pi1.GPIO_2, Grove1.SDA
  N13: Raspberry_Pi1.GPIO_3, Grove1.SCL
  GND: Raspberry_Pi1.GND, VCC1.-, Grove1.GND

notes:
  Wii Nunchuck i2c interface
  Left Channel
  Right Channel
